// Logisim project TP01 3ra parte.circ as structural Verilog: 1 circuit, main circuit Enunciado00
module Enunciado00 (
  input  D
);

  wire and_2_out, and_out, CK_out, or_out;

  Clock CK (.out(CK_out));
  and \and  (and_out, D, CK_out);
  and and_2 (and_2_out, ~CK_out, or_out);  // AND_Gate
  or \or  (or_out, and_out, and_2_out);

  // Notes on the sheet:
  //   d=0/1
  //   c=1
  //   z0=0/1
  //   z1=0
  //   q=0/1
endmodule
