// Logisim project TP01 4ta parte.circ as structural Verilog: 1 circuit, main circuit Enunciado00
module Enunciado00 (
  input  D
);

  wire and_1_out, and_2_out, and_3_out, and_4_out, CK_out, not_1_out, or_1_out, or_2_out;

  Clock CK (.out(CK_out));
  not not_1 (not_1_out, CK_out);
  D_Flip_Flop d_ff_1 ();  // open: clk, D, Q, Qn, preset, en, reset
  and and_1 (and_1_out, D, not_1_out);
  and and_2 (and_2_out, ~not_1_out, or_1_out);  // AND_Gate
  or or_1 (or_1_out, and_1_out, and_2_out);
  and and_3 (and_3_out, or_1_out, CK_out);
  and and_4 (and_4_out, ~CK_out, or_2_out);  // AND_Gate
  or or_2 (or_2_out, and_3_out, and_4_out);
endmodule
