// Logisim project Unidad 1 TP1 2da Parte.circ as structural Verilog: 2 circuits, main circuit P06
module P06 (
  input  A0,
  input  A1,
  input  B0,
  input  B1,
  output Z0,
  output Z1,
  output Z2,
  output Z3
);

  wire and_2_out, and_3_out, and_4_out, and_5_out, and_6_out, and_7_out, and_8_out, and_9_out;

  and and_1 (Z0, A0, A1, B0, B1);
  and and_2 (and_2_out, A0, ~A1, B0, ~B1);  // AND_Gate
  and and_3 (and_3_out, A0, ~A1, B0, B1);  // AND_Gate
  and and_4 (and_4_out, A0, A1, B0, ~B1);  // AND_Gate
  and and_5 (and_5_out, ~A0, A1, B0, ~B1);  // AND_Gate
  and and_6 (and_6_out, A0, ~A1, ~B0, B1);  // AND_Gate
  and and_7 (and_7_out, A0, A1, ~B0, B1);  // AND_Gate
  and and_8 (and_8_out, ~A0, A1, B0, B1);  // AND_Gate
  and and_9 (and_9_out, ~A0, A1, ~B0, B1);  // AND_Gate
  or or_1 (Z1, and_2_out, and_3_out, and_4_out);
  or or_2 (Z2, and_4_out, and_3_out, and_5_out, and_6_out, and_7_out, and_8_out);
  or or_3 (Z3, Z0, and_7_out, and_8_out, and_9_out);
endmodule

module P07 (
  input  Control,
  input  [3:0] A,
  input  [3:0] S,
  input  Carry_Out,
  input  [3:0] B
);

  wire adder_1_cout, adder_2_cout, adder_3_cout;

  // XOR_Gate xor_1 is placed but not wired
  // XOR_Gate xor_2 is placed but not wired
  // XOR_Gate xor_3 is placed but not wired
  // XOR_Gate xor_4 is placed but not wired
  Adder #(.width(1)) adder_1 (.out(S[0]), .cin(Control), .cout(adder_1_cout));  // open: a, b
  Adder #(.width(1)) adder_2 (.out(S[1]), .cin(adder_1_cout), .cout(adder_2_cout));  // open: a, b
  Adder #(.width(1)) adder_3 (.out(S[2]), .cin(adder_2_cout), .cout(adder_3_cout));  // open: a, b
  Adder #(.width(1)) adder_4 (.out(S[3]), .cin(adder_3_cout), .cout(Carry_Out));  // open: a, b
endmodule
